// Logisim project ALU(2bits).circ as structural Verilog: 5 circuits, main circuit ADDER
module ADDER (
  input  A,
  input  B,
  input  C,
  output Sum,
  output Carry
);

  wire and_1_out, and_2_out, xor_1_out, xor_2_out;

  and and_1 (and_1_out, A, B);
  xor xor_1 (xor_1_out, A, B);
  xor xor_2 (xor_2_out, A, B);
  and and_2 (and_2_out, xor_2_out, C);
  xor xor_3 (Sum, xor_1_out, C);
  or or_1 (Carry, and_1_out, and_2_out);

  // Notes on the sheet:
  //   FULL ADDER(USING XOR)
endmodule

module MUX (
  input  S1,
  input  I0,
  input  I1,
  output Output
);

  wire and_1_out, and_2_out, not_1_out;

  not not_1 (not_1_out, S1);
  and and_1 (and_1_out, I0, not_1_out);
  and and_2 (and_2_out, S1, I1);
  or or_1 (Output, and_1_out, and_2_out);

  // Notes on the sheet:
  //   2 x 1 Multiplexer
endmodule

module SUB (
  input  Binvert,
  input  CARRYin,
  input  A,
  input  B,
  output Output,
  output Carry_Addition,
  output Borrow_Subtraction
);

  wire mux_1_output, not_1_out;

  not not_1 (not_1_out, B);
  MUX mux_1 (.I0(B), .I1(not_1_out), .S1(Binvert), .Output(mux_1_output));
  ADDER adder_1 (.A(A), .B(mux_1_output), .C(CARRYin), .Sum(Output), .Carry(Carry_Addition));
  and and_1 (Borrow_Subtraction, B, Output);
endmodule

module ALU (
  input  Binvert,
  input  CarryIn,
  input  A,
  input  B,
  input  Lesser,
  input  [1:0] Selection_Lines,
  output out_7
);

  wire and_1_out, or_1_out, sub_1_output;

  and and_1 (and_1_out, A, B);
  or or_1 (or_1_out, A, B);
  SUB sub_1 (
    .A(A), .B(B), .Binvert(Binvert), .CARRYin(CarryIn), .Output(sub_1_output));  // open: Carry_Addition, Borrow_Subtraction
  _4_mux u_4_mux_1 (
    .X0(and_1_out), .X1(or_1_out), .X2(sub_1_output), .S0(Selection_Lines[0]), .X3(Lesser),
    .S1(Selection_Lines[1]), .OUTPUT(out_7));
endmodule

module _4_mux (
  input  X0,
  input  X1,
  input  X2,
  input  S0,
  input  X3,
  input  S1,
  output OUTPUT
);

  wire mux_1_output, mux_2_output;

  MUX mux_1 (.I0(X0), .I1(X1), .S1(S0), .Output(mux_1_output));
  MUX mux_2 (.I0(X2), .I1(X3), .S1(S0), .Output(mux_2_output));
  MUX mux_3 (.I0(mux_1_output), .I1(mux_2_output), .S1(S1), .Output(OUTPUT));

  // Notes on the sheet:
  //   4 X 1 MULTIPLEXER 
endmodule
