// Logisim project ALU(Standard Approach).circ as structural Verilog: 1 circuit, main circuit main
module main (
  input  Ain,
  input  Less,
  input  A,
  input  [1:0] ALUop,
  input  in_5,
  input  B,
  input  Cin,
  output Result,
  output Overflow,
  output Set,
  output out_11
);

  wire adder_1_out, and_1_out, multiplexer_1_out, multiplexer_2_out, not_1_out, not_2_out, or_1_out;

  not not_1 (not_1_out, A);
  not not_2 (not_2_out, B);
  Multiplexer #(.enable("false")) multiplexer_1 (.in0(A), .in1(not_1_out), .out(multiplexer_1_out), .sel(Ain));
  Multiplexer #(.enable("false")) multiplexer_2 (.in0(B), .in1(not_2_out), .out(multiplexer_2_out), .sel(in_5));
  and and_1 (and_1_out, multiplexer_1_out, multiplexer_2_out);
  or or_1 (or_1_out, multiplexer_1_out, multiplexer_2_out);
  Adder #(.width(1)) adder_1 (
    .a(multiplexer_1_out), .b(multiplexer_2_out), .out(adder_1_out), .cin(Cin), .cout(out_11));
  Multiplexer #(.select(2), .enable("false")) multiplexer_3 (
    .in0(and_1_out), .in1(or_1_out), .in2(adder_1_out), .in3(Less), .out(Result), .sel(ALUop));
  xor xor_1 (Overflow, Cin, out_11);
  xor xor_2 (Set, Overflow, adder_1_out);
endmodule
