// Logisim project FULL ADDER XOR.circ as structural Verilog: 3 circuits, main circuit ADDER
module ADDER (
  input  A,
  input  B,
  input  C,
  output Sum,
  output Carry
);

  wire and_1_out, and_2_out, xor_1_out, xor_2_out;

  and and_1 (and_1_out, A, B);
  xor xor_1 (xor_1_out, A, B);
  xor xor_2 (xor_2_out, A, B);
  and and_2 (and_2_out, xor_2_out, C);
  xor xor_3 (Sum, xor_1_out, C);
  or or_1 (Carry, and_1_out, and_2_out);

  // Notes on the sheet:
  //   FULL ADDER(USING XOR)
endmodule

module MUX (
  input  S1,
  input  I0,
  input  I1,
  output Output
);

  wire and_1_out, and_2_out, not_1_out;

  not not_1 (not_1_out, S1);
  and and_1 (and_1_out, I0, not_1_out);
  and and_2 (and_2_out, S1, I1);
  or or_1 (Output, and_1_out, and_2_out);

  // Notes on the sheet:
  //   2 x 1 Multiplexer
endmodule

module SUB (
  input  Binvert,
  input  CARRYin,
  input  A,
  input  B,
  output Output,
  output Carry_Addition,
  output Borrow_Subtraction
);

  wire mux_1_output, not_1_out;

  not not_1 (not_1_out, B);
  MUX mux_1 (.I0(B), .I1(not_1_out), .S1(Binvert), .Output(mux_1_output));
  ADDER adder_1 (.A(A), .B(mux_1_output), .C(CARRYin), .Sum(Output), .Carry(Carry_Addition));
  and and_1 (Borrow_Subtraction, B, Output);
endmodule
