// Logisim project FULL ADDER.circ as structural Verilog: 1 circuit, main circuit main
module main (
  input  A,
  input  B,
  input  Cin,
  output SUM,
  output CARRY
);

  wire A_prime_B_prime_C_out, A_prime_BC_prime_out, AB_out, AB_prime_C_prime_out, ABC_out, AC_out, BC_out,
       not_1_out, not_2_out, not_3_out;

  not not_1 (not_1_out, A);
  not not_2 (not_2_out, B);
  not not_3 (not_3_out, Cin);
  and A_prime_B_prime_C (A_prime_B_prime_C_out, not_1_out, not_2_out, Cin);
  and ABC (ABC_out, A, B, Cin);
  and A_prime_BC_prime (A_prime_BC_prime_out, not_1_out, B, not_3_out);
  and AB_prime_C_prime (AB_prime_C_prime_out, A, not_2_out, not_3_out);
  and AB (AB_out, A, B);
  and BC (BC_out, B, Cin);
  and AC (AC_out, A, Cin);
  or or_1 (SUM, A_prime_B_prime_C_out, ABC_out, A_prime_BC_prime_out, AB_prime_C_prime_out);
  or or_2 (CARRY, AB_out, BC_out, AC_out);

  // Notes on the sheet:
  //   FULL ADDER
endmodule
