// Logisim project Full Adder using half adder.circ as structural Verilog
module main (
  input  A,
  input  B,
  output S,
  output C
);

  xor xor_1 (S, A, B);
  and and_1 (C, A, B);

  // Notes on the sheet:
  //   HALF ADDER
endmodule

module Half_Adder (
  input  A,
  input  B,
  input  Cin,
  output SUM,
  output CARRY
);

  wire main_1_c, main_1_s, main_2_c;

  main main_1 (.A(A), .B(B), .S(main_1_s), .C(main_1_c));
  main main_2 (.A(main_1_s), .B(Cin), .S(SUM), .C(main_2_c));
  or or_1 (CARRY, main_2_c, main_1_c);
endmodule
