// Logisim project MIPSDatapath.circ as structural Verilog: 14 circuits, main circuit 1 bit ALU
module _1_bit_ALU (
  input  Cin,
  input  [1:0] OP,
  input  Ain,
  input  Bin,
  input  A,
  input  B,
  input  Less,
  output Result,
  output Cout,
  output Set
);

  wire adder_1_out, and_1_out, multiplexer_1_out, multiplexer_2_out, not_1_out, not_2_out, or_1_out,
       xor_1_out;

  not not_1 (not_1_out, A);
  not not_2 (not_2_out, B);
  Multiplexer #(.enable("false")) multiplexer_1 (.in0(A), .in1(not_1_out), .out(multiplexer_1_out), .sel(Ain));
  Multiplexer #(.enable("false")) multiplexer_2 (.in0(B), .in1(not_2_out), .out(multiplexer_2_out), .sel(Bin));
  Adder #(.width(1)) adder_1 (.a(multiplexer_1_out), .b(multiplexer_2_out), .out(adder_1_out), .cin(Cin), .cout(Cout));
  and and_1 (and_1_out, multiplexer_1_out, multiplexer_2_out);
  or or_1 (or_1_out, multiplexer_1_out, multiplexer_2_out);
  xor xor_1 (xor_1_out, Cout, Cin);
  Multiplexer #(.select(2), .enable("false")) multiplexer_3 (
    .in0(and_1_out), .in1(or_1_out), .in2(adder_1_out), .in3(Less), .out(Result), .sel(OP));
  xor xor_2 (Set, adder_1_out, xor_1_out);
endmodule

module _8bit_ALU (
  input  Ain,
  input  Bin,
  input  Cin,
  input  [1:0] OP,
  input  Less0,
  input  [7:0] A,
  input  [7:0] B,
  input  Less,
  output [7:0] Result,
  output Cout,
  output Set
);

  wire n1_bit_alu_1_cout, n1_bit_alu_2_cout, n1_bit_alu_3_cout, n1_bit_alu_4_cout, n1_bit_alu_5_cout,
       n1_bit_alu_6_cout, n1_bit_alu_7_cout;

  _1_bit_ALU u_1_bit_alu_1 (
    .A(A[0]), .B(B[0]), .Less(Less0), .Ain(Ain), .Bin(Bin), .Cin(Cin), .OP(OP), .Result(Result[0]),
    .Cout(n1_bit_alu_1_cout));  // open: Set
  _1_bit_ALU u_1_bit_alu_2 (
    .A(A[1]), .B(B[1]), .Less(Less), .Ain(Ain), .Bin(Bin), .Cin(n1_bit_alu_1_cout), .OP(OP),
    .Result(Result[1]), .Cout(n1_bit_alu_2_cout));  // open: Set
  _1_bit_ALU u_1_bit_alu_3 (
    .A(A[2]), .B(B[2]), .Less(Less), .Ain(Ain), .Bin(Bin), .Cin(n1_bit_alu_2_cout), .OP(OP),
    .Result(Result[2]), .Cout(n1_bit_alu_3_cout));  // open: Set
  _1_bit_ALU u_1_bit_alu_4 (
    .A(A[3]), .B(B[3]), .Less(Less), .Ain(Ain), .Bin(Bin), .Cin(n1_bit_alu_3_cout), .OP(OP),
    .Result(Result[3]), .Cout(n1_bit_alu_4_cout));  // open: Set
  _1_bit_ALU u_1_bit_alu_5 (
    .A(A[4]), .B(B[4]), .Less(Less), .Ain(Ain), .Bin(Bin), .Cin(n1_bit_alu_4_cout), .OP(OP),
    .Result(Result[4]), .Cout(n1_bit_alu_5_cout));  // open: Set
  _1_bit_ALU u_1_bit_alu_6 (
    .A(A[5]), .B(B[5]), .Less(Less), .Ain(Ain), .Bin(Bin), .Cin(n1_bit_alu_5_cout), .OP(OP),
    .Result(Result[5]), .Cout(n1_bit_alu_6_cout));  // open: Set
  _1_bit_ALU u_1_bit_alu_7 (
    .A(A[6]), .B(B[6]), .Less(Less), .Ain(Ain), .Bin(Bin), .Cin(n1_bit_alu_6_cout), .OP(OP),
    .Result(Result[6]), .Cout(n1_bit_alu_7_cout));  // open: Set
  _1_bit_ALU u_1_bit_alu_8 (
    .A(A[7]), .B(B[7]), .Less(Less), .Ain(Ain), .Bin(Bin), .Cin(n1_bit_alu_7_cout), .OP(OP),
    .Result(Result[7]), .Cout(Cout), .Set(Set));
endmodule

// ALU
module _32_bit_ALU (
  input  [3:0] ALUOP,
  input  [31:0] in_2,
  input  [31:0] in_3,
  output [31:0] Result,
  output ZERO
);

  wire n8bit_alu_1_cout, n8bit_alu_2_cout, n8bit_alu_3_cout, n8bit_alu_4_set, or_1_out;

  _8bit_ALU u_8bit_alu_1 (
    .Less0(n8bit_alu_4_set), .A(in_2[7:0]), .B(in_3[7:0]), .Less(1'b0), .Ain(ALUOP[3]), .Bin(ALUOP[2]),
    .Cin(ALUOP[2]), .OP(ALUOP[1:0]), .Result(Result[7:0]), .Cout(n8bit_alu_1_cout));  // open: Set
  _8bit_ALU u_8bit_alu_2 (
    .Less0(1'b0), .A(in_2[15:8]), .B(in_3[15:8]), .Less(1'b0), .Ain(ALUOP[3]), .Bin(ALUOP[2]),
    .Cin(n8bit_alu_1_cout), .OP(ALUOP[1:0]), .Result(Result[15:8]), .Cout(n8bit_alu_2_cout));  // open: Set
  _8bit_ALU u_8bit_alu_3 (
    .Less0(1'b0), .A(in_2[23:16]), .B(in_3[23:16]), .Less(1'b0), .Ain(ALUOP[3]), .Bin(ALUOP[2]),
    .Cin(n8bit_alu_2_cout), .OP(ALUOP[1:0]), .Result(Result[23:16]), .Cout(n8bit_alu_3_cout));  // open: Set
  _8bit_ALU u_8bit_alu_4 (
    .Less0(1'b0), .A(in_2[31:24]), .B(in_3[31:24]), .Less(1'b0), .Ain(ALUOP[3]), .Bin(ALUOP[2]),
    .Cin(n8bit_alu_3_cout), .OP(ALUOP[1:0]), .Result(Result[31:24]), .Set(n8bit_alu_4_set));  // open: Cout
  or or_1 (or_1_out, Result[0], Result[1], Result[2], Result[3], Result[4], Result[5], Result[6], Result[7], Result[8], Result[9], Result[10], Result[11], Result[12], Result[13], Result[14], Result[15], Result[16], Result[17], Result[18], Result[19], Result[20], Result[21], Result[22], Result[23], Result[24], Result[25], Result[26], Result[27], Result[28], Result[29], Result[30], Result[31]);
  not not_1 (ZERO, or_1_out);

  // Notes on the sheet:
  //   AinBinop1op2
endmodule

// MC
module Control_Unit (
  input  [5:0] in_1,
  output dstReg,
  output RegWrite,
  output MemRead,
  output ALUsrc,
  output MemToReg,
  output MemWrite,
  output beq,
  output [1:0] op,
  output jmp
);

  and and_1 (dstReg, ~in_1[5], ~in_1[4], ~in_1[3], ~in_1[2], ~in_1[1], ~in_1[0]);  // AND_Gate
  and and_2 (MemRead, in_1[5], ~in_1[4], ~in_1[3], ~in_1[2], in_1[1], in_1[0]);  // AND_Gate
  and and_3 (MemWrite, in_1[5], ~in_1[4], in_1[3], ~in_1[2], in_1[1], in_1[0]);  // AND_Gate
  or or_1 (RegWrite, MemRead, dstReg);
  or or_2 (ALUsrc, MemRead, MemWrite);
  and and_4 (beq, ~in_1[5], ~in_1[4], ~in_1[3], in_1[2], ~in_1[1], ~in_1[0]);  // AND_Gate
  and and_5 (jmp, ~in_1[5], ~in_1[4], ~in_1[3], ~in_1[2], in_1[1], ~in_1[0]);  // AND_Gate
  or or_3 (op[1], dstReg, jmp);
  or or_4 (op[0], jmp, beq);

  assign MemToReg = MemRead;

  // Notes on the sheet:
  //   R-type
  //   lw
  //   sw
  //   beq
  //   jmp
endmodule

// AC
module ALUControl (
  input  [1:0] op,
  input  [5:0] \function ,
  output [3:0] ALUop
);

  wire and_1_out, and_2_out, or_1_out, or_4_out;

  or or_1 (or_1_out, \function [2], \function [5]);
  and and_1 (and_1_out, op[1], \function [3]);
  or or_2 (ALUop[1], ~\function [4], ~op[1]);  // OR_Gate
  or or_3 (ALUop[2], op[0], and_1_out);
  and and_2 (and_2_out, op[1], or_1_out);
  or or_4 (or_4_out, and_2_out, ~\function [3]);  // OR_Gate
  and and_3 (ALUop[3], ALUop[2], ~ALUop[1]);  // AND_Gate
  and and_4 (ALUop[0], and_2_out, or_4_out);
endmodule

module \reg  (
  input  [31:0] Data,
  input  RegWrite,
  input  Write_Register,
  output [31:0] data_out
);

  wire and_1_out, clock_1_out;

  and and_1 (and_1_out, RegWrite, Write_Register);
  Clock clock_1 (.out(clock_1_out));
  Register #(.width(32)) register_1 (.D(Data), .en(and_1_out), .Q(data_out), .clk(clock_1_out));  // open: clr
endmodule

// RF
module Regfile (
  input  RegWrite,
  input  [4:0] Write_Register,
  input  [31:0] Data,
  input  [4:0] RR1,
  input  [4:0] RR2,
  output [31:0] Read1,
  output [31:0] Read2
);

  wire [7:0] decoder_1_out0, decoder_1_out8, decoder_1_out16, decoder_1_out24;
  wire [31:0] reg_1_data_out, reg_2_data_out, reg_3_data_out, reg_4_data_out, reg_5_data_out, reg_6_data_out,
       reg_7_data_out, reg_8_data_out, reg_9_data_out, reg_10_data_out, reg_11_data_out, reg_12_data_out,
       reg_13_data_out, reg_14_data_out, reg_15_data_out, reg_16_data_out, reg_17_data_out, reg_18_data_out,
       reg_19_data_out, reg_20_data_out, reg_21_data_out, reg_22_data_out, reg_23_data_out, reg_24_data_out,
       reg_25_data_out, reg_26_data_out, reg_27_data_out, reg_28_data_out, reg_29_data_out, reg_30_data_out,
       reg_31_data_out, reg_32_data_out;

  Decoder #(.select(5), .enable("false")) decoder_1 (
    .out0(decoder_1_out0[0]), .out1(decoder_1_out0[1]), .out2(decoder_1_out0[2]), .out3(decoder_1_out0[3]),
    .out4(decoder_1_out0[4]), .out5(decoder_1_out0[5]), .out6(decoder_1_out0[6]), .out7(decoder_1_out0[7]),
    .out8(decoder_1_out8[0]), .out9(decoder_1_out8[1]), .out10(decoder_1_out8[2]), .out11(decoder_1_out8[3]),
    .out12(decoder_1_out8[4]), .out13(decoder_1_out8[5]), .out14(decoder_1_out8[6]),
    .out15(decoder_1_out8[7]), .out16(decoder_1_out16[0]), .out17(decoder_1_out16[1]),
    .out18(decoder_1_out16[2]), .out19(decoder_1_out16[3]), .out20(decoder_1_out16[4]),
    .out21(decoder_1_out16[5]), .out22(decoder_1_out16[6]), .out23(decoder_1_out16[7]),
    .out24(decoder_1_out24[0]), .out25(decoder_1_out24[1]), .out26(decoder_1_out24[2]),
    .out27(decoder_1_out24[3]), .out28(decoder_1_out24[4]), .out29(decoder_1_out24[5]),
    .out30(decoder_1_out24[6]), .out31(decoder_1_out24[7]), .sel(Write_Register));
  \reg  reg_1 (.Data(Data), .RegWrite(RegWrite), .Write_Register(decoder_1_out0[0]), .data_out(reg_1_data_out));
  \reg  reg_2 (.Data(Data), .RegWrite(RegWrite), .Write_Register(decoder_1_out0[1]), .data_out(reg_2_data_out));
  \reg  reg_3 (.Data(Data), .RegWrite(RegWrite), .Write_Register(decoder_1_out0[2]), .data_out(reg_3_data_out));
  \reg  reg_4 (.Data(Data), .RegWrite(RegWrite), .Write_Register(decoder_1_out0[3]), .data_out(reg_4_data_out));
  \reg  reg_5 (.Data(Data), .RegWrite(RegWrite), .Write_Register(decoder_1_out0[4]), .data_out(reg_5_data_out));
  \reg  reg_6 (.Data(Data), .RegWrite(RegWrite), .Write_Register(decoder_1_out0[5]), .data_out(reg_6_data_out));
  \reg  reg_7 (.Data(Data), .RegWrite(RegWrite), .Write_Register(decoder_1_out0[6]), .data_out(reg_7_data_out));
  \reg  reg_8 (.Data(Data), .RegWrite(RegWrite), .Write_Register(decoder_1_out0[7]), .data_out(reg_8_data_out));
  \reg  reg_9 (.Data(Data), .RegWrite(RegWrite), .Write_Register(decoder_1_out8[0]), .data_out(reg_9_data_out));
  \reg  reg_10 (.Data(Data), .RegWrite(RegWrite), .Write_Register(decoder_1_out8[1]), .data_out(reg_10_data_out));
  \reg  reg_11 (.Data(Data), .RegWrite(RegWrite), .Write_Register(decoder_1_out8[2]), .data_out(reg_11_data_out));
  \reg  reg_12 (.Data(Data), .RegWrite(RegWrite), .Write_Register(decoder_1_out8[3]), .data_out(reg_12_data_out));
  \reg  reg_13 (.Data(Data), .RegWrite(RegWrite), .Write_Register(decoder_1_out8[4]), .data_out(reg_13_data_out));
  \reg  reg_14 (.Data(Data), .RegWrite(RegWrite), .Write_Register(decoder_1_out8[5]), .data_out(reg_14_data_out));
  \reg  reg_15 (.Data(Data), .RegWrite(RegWrite), .Write_Register(decoder_1_out8[6]), .data_out(reg_15_data_out));
  \reg  reg_16 (.Data(Data), .RegWrite(RegWrite), .Write_Register(decoder_1_out8[7]), .data_out(reg_16_data_out));
  \reg  reg_17 (.Data(Data), .RegWrite(RegWrite), .Write_Register(decoder_1_out16[0]), .data_out(reg_17_data_out));
  \reg  reg_18 (.Data(Data), .RegWrite(RegWrite), .Write_Register(decoder_1_out16[1]), .data_out(reg_18_data_out));
  \reg  reg_19 (.Data(Data), .RegWrite(RegWrite), .Write_Register(decoder_1_out16[2]), .data_out(reg_19_data_out));
  \reg  reg_20 (.Data(Data), .RegWrite(RegWrite), .Write_Register(decoder_1_out16[3]), .data_out(reg_20_data_out));
  \reg  reg_21 (.Data(Data), .RegWrite(RegWrite), .Write_Register(decoder_1_out16[4]), .data_out(reg_21_data_out));
  \reg  reg_22 (.Data(Data), .RegWrite(RegWrite), .Write_Register(decoder_1_out16[5]), .data_out(reg_22_data_out));
  \reg  reg_23 (.Data(Data), .RegWrite(RegWrite), .Write_Register(decoder_1_out16[6]), .data_out(reg_23_data_out));
  \reg  reg_24 (.Data(Data), .RegWrite(RegWrite), .Write_Register(decoder_1_out16[7]), .data_out(reg_24_data_out));
  \reg  reg_25 (.Data(Data), .RegWrite(RegWrite), .Write_Register(decoder_1_out24[0]), .data_out(reg_25_data_out));
  \reg  reg_26 (.Data(Data), .RegWrite(RegWrite), .Write_Register(decoder_1_out24[1]), .data_out(reg_26_data_out));
  \reg  reg_27 (.Data(Data), .RegWrite(RegWrite), .Write_Register(decoder_1_out24[2]), .data_out(reg_27_data_out));
  \reg  reg_28 (.Data(Data), .RegWrite(RegWrite), .Write_Register(decoder_1_out24[3]), .data_out(reg_28_data_out));
  \reg  reg_29 (.Data(Data), .RegWrite(RegWrite), .Write_Register(decoder_1_out24[4]), .data_out(reg_29_data_out));
  \reg  reg_30 (.Data(Data), .RegWrite(RegWrite), .Write_Register(decoder_1_out24[5]), .data_out(reg_30_data_out));
  \reg  reg_31 (.Data(Data), .RegWrite(RegWrite), .Write_Register(decoder_1_out24[6]), .data_out(reg_31_data_out));
  \reg  reg_32 (.Data(Data), .RegWrite(RegWrite), .Write_Register(decoder_1_out24[7]), .data_out(reg_32_data_out));
  Multiplexer #(.select(5), .width(32), .enable("false")) multiplexer_1 (
    .in0(reg_1_data_out), .in1(reg_2_data_out), .in2(reg_3_data_out), .in3(reg_4_data_out),
    .in4(reg_5_data_out), .in5(reg_6_data_out), .in6(reg_7_data_out), .in7(reg_8_data_out),
    .in8(reg_9_data_out), .in9(reg_10_data_out), .in10(reg_11_data_out), .in11(reg_12_data_out),
    .in12(reg_13_data_out), .in13(reg_14_data_out), .in14(reg_15_data_out), .in15(reg_16_data_out),
    .in16(reg_17_data_out), .in17(reg_18_data_out), .in18(reg_19_data_out), .in19(reg_20_data_out),
    .in20(reg_21_data_out), .in21(reg_22_data_out), .in22(reg_23_data_out), .in23(reg_24_data_out),
    .in24(reg_25_data_out), .in25(reg_26_data_out), .in26(reg_27_data_out), .in27(reg_28_data_out),
    .in28(reg_29_data_out), .in29(reg_30_data_out), .in30(reg_31_data_out), .in31(reg_32_data_out),
    .out(Read1), .sel(RR1));
  Multiplexer #(.select(5), .width(32), .enable("false")) multiplexer_2 (
    .in0(reg_1_data_out), .in1(reg_2_data_out), .in2(reg_3_data_out), .in3(reg_4_data_out),
    .in4(reg_5_data_out), .in5(reg_6_data_out), .in6(reg_7_data_out), .in7(reg_8_data_out),
    .in8(reg_9_data_out), .in9(reg_10_data_out), .in10(reg_11_data_out), .in11(reg_12_data_out),
    .in12(reg_13_data_out), .in13(reg_14_data_out), .in14(reg_15_data_out), .in15(reg_16_data_out),
    .in16(reg_17_data_out), .in17(reg_18_data_out), .in18(reg_19_data_out), .in19(reg_20_data_out),
    .in20(reg_21_data_out), .in21(reg_22_data_out), .in22(reg_23_data_out), .in23(reg_24_data_out),
    .in24(reg_25_data_out), .in25(reg_26_data_out), .in26(reg_27_data_out), .in27(reg_28_data_out),
    .in28(reg_29_data_out), .in29(reg_30_data_out), .in30(reg_31_data_out), .in31(reg_32_data_out),
    .out(Read2), .sel(RR2));
endmodule

// cov
module covert (
  input  [31:0] in_1,
  output [4:0] out_2
);


  assign out_2 = in_1[6:2];
endmodule

// sinE
module signExt (
  input  [15:0] in_1,
  output [31:0] out_2
);


  assign out_2 = {{17{in_1[15]}}, in_1[14:0]};
endmodule

// con
module concate (
  input  [25:0] _0_25in,
  input  [31:0] pc_4,
  output [31:0] _32out
);


  assign _32out = {pc_4[31:28], _0_25in, 2'b00};
endmodule

// >>
module leftShit (
  input  [31:0] in,
  output [31:0] out
);


  assign out = {in[29:0], 2'b00};
endmodule

// Pc
module PC (
  input  [31:0] pcin,
  input  Clear,
  output [31:0] pcout
);

  wire clock_1_out;

  Clock clock_1 (.out(clock_1_out));
  Register #(.width(32)) register_1 (.D(pcin), .Q(pcout), .clk(clock_1_out), .clr(Clear));  // open: en
endmodule

module MIPS_Single_Cycle (
  input  in_1
);

  wire and_1_out, clock_1_out, control_unit_1_alusrc, control_unit_1_beq, control_unit_1_dstreg,
       control_unit_1_jmp, control_unit_1_memread, control_unit_1_memtoreg, control_unit_1_memwrite,
       control_unit_1_regwrite, n32_bit_alu_1_zero;
  wire [1:0] control_unit_1_op;
  wire [3:0] alucontrol_1_aluop;
  wire [4:0] covert_1_out_2, covert_2_out_2, multiplexer_1_out;
  wire [31:0] adder_1_out, adder_2_out, concate_1__32out, leftshit_1_out, multiplexer_2_out,
       multiplexer_3_out, multiplexer_4_out, multiplexer_5_out, n32_bit_alu_1_result, pc_1_pcout, ram_1_data,
       regfile_1_read1, regfile_1_read2, rom_1_data, signext_1_out_2;

  PC pc_1 (.pcin(multiplexer_4_out), .Clear(in_1), .pcout(pc_1_pcout));
  covert covert_1 (.in_1(pc_1_pcout), .out_2(covert_1_out_2));
  Adder #(.width(32)) adder_1 (.a(32'h4), .b(pc_1_pcout), .out(adder_1_out));  // open: cin, cout
  Control_Unit control_unit_1 (
    .in_1(rom_1_data[31:26]), .dstReg(control_unit_1_dstreg), .RegWrite(control_unit_1_regwrite),
    .MemRead(control_unit_1_memread), .ALUsrc(control_unit_1_alusrc), .MemToReg(control_unit_1_memtoreg),
    .MemWrite(control_unit_1_memwrite), .beq(control_unit_1_beq), .op(control_unit_1_op),
    .jmp(control_unit_1_jmp));
  ROM #(.addrWidth(5), .dataWidth(32)) rom_1 (.addr(covert_1_out_2), .data(rom_1_data));  // open: sel
  Multiplexer #(.width(5), .enable("false")) multiplexer_1 (
    .in0(rom_1_data[20:16]), .in1(rom_1_data[15:11]), .out(multiplexer_1_out), .sel(control_unit_1_dstreg));
  Regfile regfile_1 (
    .RegWrite(control_unit_1_regwrite), .Write_Register(multiplexer_1_out), .Data(multiplexer_5_out),
    .Read1(regfile_1_read1), .Read2(regfile_1_read2), .RR1(rom_1_data[25:21]), .RR2(rom_1_data[20:16]));
  signExt signext_1 (.in_1(rom_1_data[15:0]), .out_2(signext_1_out_2));
  leftShit leftshit_1 (.in(signext_1_out_2), .out(leftshit_1_out));
  Multiplexer #(.width(32), .enable("false")) multiplexer_2 (
    .in0(regfile_1_read2), .in1(signext_1_out_2), .out(multiplexer_2_out), .sel(control_unit_1_alusrc));
  ALUControl alucontrol_1 (.op(control_unit_1_op), .\function (rom_1_data[5:0]), .ALUop(alucontrol_1_aluop));
  concate concate_1 (._0_25in(rom_1_data[25:0]), .pc_4(adder_1_out), ._32out(concate_1__32out));
  Adder #(.width(32)) adder_2 (.a(adder_1_out), .b(leftshit_1_out), .out(adder_2_out));  // open: cin, cout
  _32_bit_ALU u_32_bit_alu_1 (
    .in_2(regfile_1_read1), .in_3(multiplexer_2_out), .Result(n32_bit_alu_1_result),
    .ZERO(n32_bit_alu_1_zero), .ALUOP(alucontrol_1_aluop));
  Multiplexer #(.width(32), .enable("false")) multiplexer_3 (
    .in0(adder_1_out), .in1(adder_2_out), .out(multiplexer_3_out), .sel(and_1_out));
  and and_1 (and_1_out, control_unit_1_beq, n32_bit_alu_1_zero);
  covert covert_2 (.in_1(n32_bit_alu_1_result), .out_2(covert_2_out_2));
  Multiplexer #(.width(32), .enable("false")) multiplexer_4 (
    .in0(multiplexer_3_out), .in1(concate_1__32out), .out(multiplexer_4_out), .sel(control_unit_1_jmp));
  RAM #(.addrWidth(5), .dataWidth(32), .bus("separate")) ram_1 (
    .addr(covert_2_out_2), .din(regfile_1_read2), .data(ram_1_data), .str(control_unit_1_memwrite),
    .clk(clock_1_out), .ld(control_unit_1_memread));  // open: sel, clr
  Clock clock_1 (.out(clock_1_out));
  Multiplexer #(.width(32), .enable("false")) multiplexer_5 (
    .in0(n32_bit_alu_1_result), .in1(ram_1_data), .out(multiplexer_5_out), .sel(control_unit_1_memtoreg));

  // Notes on the sheet:
  //   contents of rom_1 (hex, n*v repeats v):
  //   22 8c010000 8c220000 8c230004 622024 622827 ac040004 ac050008 1000ffff
endmodule

module CombCon (
  input  [27:0] in_1,
  input  [31:0] in_2
);

  wire [5:0] undriven_2, undriven_3, undriven_4;
  wire [6:0] undriven;

  // AND_Gate and_1 has open pins: in0={undriven_4, undriven_3, undriven_2, undriven, in_1[6:0]}, in1=in_2, out=open
  // Pins of 7 and 28 bits meet at in_1
endmodule
