// Logisim project Multiplexer 2 x 1.circ as structural Verilog: 2 circuits, main circuit main
module main (
  input  S1,
  input  I0,
  input  I1,
  output Output
);

  wire and_1_out, and_2_out, not_1_out;

  not not_1 (not_1_out, S1);
  and and_1 (and_1_out, I0, not_1_out);
  and and_2 (and_2_out, S1, I1);
  or or_1 (Output, and_1_out, and_2_out);

  // Notes on the sheet:
  //   2 x 1 Multiplexer
endmodule

module _2_x_1 (
  input  S0,
  input  S1,
  input  X0,
  input  X1,
  input  X2,
  input  X3,
  output OUTPUT
);

  wire main_1_output, main_2_output;

  main main_1 (.I0(X0), .I1(X1), .S1(S1), .Output(main_1_output));
  main main_2 (.I0(X2), .I1(X3), .S1(S1), .Output(main_2_output));
  main main_3 (.I0(main_1_output), .I1(main_2_output), .S1(S0), .Output(OUTPUT));

  // Notes on the sheet:
  //   4 X 1 MULTIPLEXER 
endmodule
