// Logisim project Multiplexer 4 x 1.circ as structural Verilog: 2 circuits, main circuit 2 x 1
module _2_x_1 (
  input  S1,
  input  I0,
  input  I1,
  output Output
);

  wire and_1_out, and_2_out, not_1_out;

  not not_1 (not_1_out, S1);
  and and_1 (and_1_out, I0, not_1_out);
  and and_2 (and_2_out, S1, I1);
  or or_1 (Output, and_1_out, and_2_out);

  // Notes on the sheet:
  //   2 x 1 Multiplexer
endmodule

module _4_x_1 (
  input  X0,
  input  X1,
  input  X2,
  input  X3,
  input  [1:0] in_5,
  output OUTPUT
);

  wire n2_x_1_1_output, n2_x_1_2_output;

  _2_x_1 u_2_x_1_1 (.I0(X0), .I1(X1), .S1(in_5[0]), .Output(n2_x_1_1_output));
  _2_x_1 u_2_x_1_2 (.I0(X2), .I1(X3), .S1(in_5[0]), .Output(n2_x_1_2_output));
  _2_x_1 u_2_x_1_3 (.I0(n2_x_1_1_output), .I1(n2_x_1_2_output), .S1(in_5[1]), .Output(OUTPUT));

  // Notes on the sheet:
  //   4 X 1 MULTIPLEXER 
endmodule
